# Fritzing sketch 回路図_トランジスタ版 (saved by Fritzing 0.9.3b)
circuit board: 4.37cm x 3.64cm
breadboards: 1

parts:
  part = Resistor [tolerance=±5% resistance=1k package=THT]
  CH2 = mystery part, 3 pins [chip_label=SERVO]
  CH3 = mystery part, 3 pins [chip_label=SERVO]
  CH4 = mystery part, 3 pins [chip_label=SERVO]
  IC2 = IC, SIP package, 3 pins [chip_label=TA48033S]
  C1 = Electrolytic Capacitor [capacitance=47µF package="100 mil [THT, electrolytic]"]
  IC1 = IC, DIP package, 18 pins [chip_label=WROOM02]
  Q2 = NPN-Transistor [package="TO92 [THT]"]
  C2 = Ceramic Capacitor [capacitance=100nF package="100 mil [THT, multilayer]"]
  Q4 = NPN-Transistor [package="TO92 [THT]"]
  Q1 = NPN-Transistor [package="TO92 [THT]"]
  CH1 = mystery part, 3 pins [chip_label=SERVO]
  Q3 = NPN-Transistor [package="TO92 [THT]"]
  R18 = Resistor [tolerance=±5% resistance=10k package=THT]
  R19 = Resistor [tolerance=±5% resistance=10k package=THT]
  S3 = Pushbutton [package=THT]
  S4 = Pushbutton [package=THT]
  part_2 = Resistor [tolerance=±5% resistance=1k package=THT]
  part_3 = Resistor [tolerance=±5% resistance=1k package=THT]
  Batt = mystery part, 3 pins [chip_label=SERVO]
  part_4 = IC, SIP package, 5 pins [chip_label="R-array 10k"]
  part_5 = IC, SIP package, 5 pins [chip_label="R-array 10k"]
  R2 = Resistor [tolerance=±5% resistance=10k package=THT]
  part_6 = Resistor [tolerance=±5% resistance=1k package=THT]
  U6 = mystery part, 4 pins [chip_label=SERIAL]
  U7 = mystery part, 2 pins [chip_label=JP1]
  LED1 = LED - 5mm [color="Red (633nm)" package="5 mm [THT]"]
  R20 = Resistor [tolerance=±5% resistance=1k package=THT]

nets:
  3.3V: part.Pin_0, IC2.pin3, C1.+, IC1.pin1, R18.Pin_1, R19.Pin_1, part_2.Pin_0, part_3.Pin_0, part_5.pin1, part_6.Pin_0, R20.Pin_0
  N1: part.Pin_1, Q3.B
  N2: CH2.pin1, Q2.C, part_4.pin3
  5V: CH2.pin2, CH3.pin2, CH4.pin2, IC2.pin1, C2.1, CH1.pin2, Batt.pin2, part_4.pin1, U6.pin1
  GND: CH2.pin3, CH3.pin3, CH4.pin3, IC2.pin2, C1.-, IC1.pin9, C2.0, CH1.pin3, S3.leg0, S4.leg0, Batt.pin3, R2.Pin_0, U7.pin2, LED1.cathode
  N3: CH3.pin1, Q3.C, part_4.pin4
  N4: CH4.pin1, Q4.C, part_4.pin5
  N5: IC1.pin2, part_5.pin2
  N6: IC1.pin3, R18.Pin_0, S3.leg1
  N7: IC1.pin4, Q3.E
  N8: IC1.pin5, Q4.E
  N9: IC1.pin6, R2.Pin_1
  N10: IC1.pin7, part_5.pin3
  N11: IC1.pin8, part_5.pin5, U7.pin1
  N12: IC1.pin10, Q1.E
  N13: IC1.pin11, U6.pin3
  N14: IC1.pin12, U6.pin4
  N15: IC1.pin13, U6.pin2
  N16: IC1.pin14, Q2.E
  N17: IC1.pin15, part_5.pin4
  N18: IC1.pin17, R19.Pin_0, S4.leg1
  N19: Q2.B, part_3.Pin_1
  N20: Q4.B, part_2.Pin_1
  N21: Q1.B, part_6.Pin_1
  N22: Q1.C, CH1.pin1, part_4.pin2
  N23: LED1.anode, R20.Pin_1
